// Logisim project cpu.circ as structural Verilog: 1 circuit, main circuit cpu
module cpu (
  input  Rest
);

  wire alu_1_zero, alucontroller_1_sh_amount, and_1_out, and_2_out, and_3_out, and_4_out, and_5_out,
       cache_1_readfrommem, cache_1_writeinmemory, clk, comparator_1_eq, comparator_2_eq, comparator_3_eq,
       controller_1_alusrc, controller_1_branch, controller_1_jump, controller_1_memtoreg,
       controller_1_regdst, controller_1_regwren, LB, multiplexer_2_out, not_1_out, or_1_out, RType;
  wire [1:0] alu_1_result;
  wire [3:0] adder_1_out_2, bit_extender_5_out, controller_1_memwrmask, multiplexer_8_out, shifter_4_out;
  wire [4:0] alucontroller_1_alu_out, bit_extender_4_out, mem_1_memreaddata_2, mem_1_memreaddata_3,
       multiplexer_3_out, multiplexer_4_out, shifter_5_out;
  wire [5:0] mem_1_memreaddata;
  wire [7:0] multiplexer_13_out;
  wire [25:16] mem_1_memreaddata_4;
  wire [27:0] adder_1_out;
  wire [31:0] adder_2_out, bit_extender_1_out, bit_extender_2_out, bit_extender_3_out, bit_extender_6_out,
       cache_1_addressout, cache_1_readdata, cache_1_writedataout, MemData, multiplexer_1_out,
       multiplexer_5_out, multiplexer_6_out, multiplexer_7_out, multiplexer_9_out, multiplexer_10_out,
       multiplexer_11_out, multiplexer_12_out, multiplexer_14_out, multiplexer_15_out, pc, regfile_1_p7,
       regfile_1_p8, shifter_1_out, shifter_2_out, shifter_3_out, shifter_6_out, signextend_1_extended,
       undriven, xor_1_out;
  wire [31:2] alu_1_result_2;
  wire [31:26] mem_1_memreaddata_5;

  Multiplexer #(.width(32)) multiplexer_1 (
    .in0(multiplexer_11_out), .in1({alu_1_result_2, alu_1_result}), .out(multiplexer_1_out), .sel(and_3_out));
  Multiplexer multiplexer_2 (.in0(1'b1), .in1(1'b0), .out(multiplexer_2_out), .sel(and_4_out));
  Clock u_Clk (.out(clk));
  Register #(.width(32)) u_PC (.D(multiplexer_1_out), .en(multiplexer_2_out), .clk(clk), .Q(pc), .clr(Rest));
  Adder #(.width(32)) adder_1 (.a(32'h4), .b(pc), .out({adder_1_out_2, adder_1_out}));  // open: cin, cout
  mem mem_1 (
    .MemAddress(pc), .clk(clk),
    .MemReadData({mem_1_memreaddata_5, mem_1_memreaddata_4, mem_1_memreaddata_3, mem_1_memreaddata_2, mem_1_memreaddata}));  // open: MemWriteMask, MemWriteData
  Multiplexer #(.width(5)) multiplexer_3 (
    .in0(mem_1_memreaddata_4[20:16]), .in1(mem_1_memreaddata_3), .out(multiplexer_3_out),
    .sel(controller_1_regdst));
  assign bit_extender_1_out = {{6{1'b0}}, {mem_1_memreaddata_4, mem_1_memreaddata_3, mem_1_memreaddata_2, mem_1_memreaddata}};  // Bit_Extender bit_extender_1
  and and_1 (and_1_out, controller_1_jump, controller_1_regwren);
  Multiplexer #(.width(5)) multiplexer_4 (
    .in0(multiplexer_3_out), .in1({5{1'b1}}), .out(multiplexer_4_out), .sel(and_1_out));
  Multiplexer #(.width(32)) multiplexer_5 (
    .in0(multiplexer_15_out), .in1(pc), .out(multiplexer_5_out), .sel(and_1_out));
  Shifter #(.width(32)) shifter_1 (.in(bit_extender_1_out), .\dist (5'b00010), .out(shifter_1_out));
  assign bit_extender_2_out = {{28{1'b0}}, adder_1_out_2};  // Bit_Extender bit_extender_2
  assign bit_extender_3_out = {{27{1'b0}}, mem_1_memreaddata_2};  // Bit_Extender bit_extender_3
  Shifter #(.width(32)) shifter_2 (.in(bit_extender_2_out), .\dist (5'b11100), .out(shifter_2_out));
  Controller controller_1 (
    .Opcode(mem_1_memreaddata_5), .RegDst(controller_1_regdst), .Branch(controller_1_branch),
    .Jump(controller_1_jump), .RegWrEn(controller_1_regwren), .AluSrc(controller_1_alusrc),
    .MemToReg(controller_1_memtoreg), .AluOpr(RType), .MemWrMask(controller_1_memwrmask), .LB(LB));
  assign xor_1_out = shifter_1_out ^ shifter_2_out;  // XOR_Gate xor_1, 32 bits wide
  // regfile regfile_1: pin names not known; wires that end beside it: mem_1_memreaddata_4[25:21], mem_1_memreaddata_4[20:16], multiplexer_4_out, multiplexer_5_out, controller_1_regwren, clk, regfile_1_p7, regfile_1_p8
  signExtend signextend_1 (
    .Immd({mem_1_memreaddata_3, mem_1_memreaddata_2, mem_1_memreaddata}), .Extended(signextend_1_extended));
  and and_2 (and_2_out, ~controller_1_branch, controller_1_alusrc);  // AND_Gate
  Multiplexer #(.width(32)) multiplexer_6 (
    .in0(regfile_1_p7), .in1(bit_extender_3_out), .out(multiplexer_6_out), .sel(alucontroller_1_sh_amount));
  Shifter #(.width(32)) shifter_3 (.in(signextend_1_extended), .\dist (5'b00010), .out(shifter_3_out));
  Multiplexer #(.width(32)) multiplexer_7 (
    .in0(regfile_1_p8), .in1(signextend_1_extended), .out(multiplexer_7_out), .sel(and_2_out));
  assign bit_extender_4_out = {{3{1'b0}}, alu_1_result};  // Bit_Extender bit_extender_4
  AluController alucontroller_1 (
    .func(mem_1_memreaddata), .opcode(mem_1_memreaddata_5), .aluOperation(RType),
    .ALU_out(alucontroller_1_alu_out), .sh_amount(alucontroller_1_sh_amount));
  and and_3 (and_3_out, alu_1_zero, ~comparator_2_eq, RType);  // AND_Gate
  Adder #(.width(32)) adder_2 (
    .a({adder_1_out_2, adder_1_out}), .b(shifter_3_out), .out(adder_2_out));  // open: cin, cout
  Comparator #(.width(4)) comparator_1 (.a(controller_1_memwrmask), .b(4'b0001), .eq(comparator_1_eq));  // open: gt, lt
  Shifter #(.width(4)) shifter_4 (.in(controller_1_memwrmask), .\dist (alu_1_result), .out(shifter_4_out));
  Shifter #(.width(5)) shifter_5 (.in(bit_extender_4_out), .\dist (3'b011), .out(shifter_5_out));
  and and_4 (and_4_out, RType, alu_1_zero, comparator_2_eq);
  Multiplexer #(.width(4)) multiplexer_8 (
    .in0(controller_1_memwrmask), .in1(shifter_4_out), .out(multiplexer_8_out), .sel(comparator_1_eq));
  ALU alu_1 (
    .ReadData1(multiplexer_6_out), .ReadData2(multiplexer_7_out), .ControlBits(alucontroller_1_alu_out),
    .Result({alu_1_result_2, alu_1_result}), .Zero(alu_1_zero));
  Shifter #(.width(32)) shifter_6 (.in(regfile_1_p8), .\dist (shifter_5_out), .out(shifter_6_out));
  Multiplexer #(.width(32)) multiplexer_9 (
    .in0({adder_1_out_2, adder_1_out}), .in1(adder_2_out), .out(multiplexer_9_out), .sel(and_5_out));
  and and_5 (and_5_out, controller_1_branch, alu_1_zero);
  Multiplexer #(.width(32)) multiplexer_10 (
    .in0(regfile_1_p8), .in1(shifter_6_out), .out(multiplexer_10_out), .sel(comparator_1_eq));
  Multiplexer #(.width(32)) multiplexer_11 (
    .in0(xor_1_out), .in1(multiplexer_9_out), .out(multiplexer_11_out), .sel(not_1_out));
  not not_1 (not_1_out, controller_1_jump);
  Comparator #(.width(32)) comparator_2 (
    .a({alu_1_result_2, alu_1_result}), .b({32{1'b1}}), .eq(comparator_2_eq));  // open: gt, lt
  Multiplexer #(.width(32)) multiplexer_12 (
    .in0(MemData), .in1({alu_1_result_2, alu_1_result}), .out(multiplexer_12_out));  // open: sel
  Comparator #(.width(4)) comparator_3 (.a(4'b1111), .b(multiplexer_8_out), .eq(comparator_3_eq));  // open: gt, lt
  or or_1 (or_1_out, cache_1_readfrommem, comparator_3_eq);
  assign bit_extender_5_out = {{3{cache_1_writeinmemory}}, cache_1_writeinmemory};  // Bit_Extender bit_extender_5
  Cache cache_1 (
    .clk(clk), .Address(multiplexer_10_out), .WriteEnable(or_1_out), .WriteData(multiplexer_12_out),
    .ReadFromMem(cache_1_readfrommem), .ReadData(cache_1_readdata), .AddressOut(cache_1_addressout),
    .WriteInMemory(cache_1_writeinmemory), .WriteDataOut(cache_1_writedataout));  // open: HIT
  memDelayed memdelayed_1 (
    .MemAddress(cache_1_addressout), .MemWriteMask(bit_extender_5_out), .MemWriteData(cache_1_writedataout),
    .clk(clk), .MemReadData(MemData));
  Multiplexer #(.select(2), .width(8)) multiplexer_13 (
    .in0(undriven[7:0]), .in1(undriven[15:8]), .in2(undriven[23:16]), .in3(undriven[31:24]),
    .out(multiplexer_13_out), .sel(alu_1_result));
  Multiplexer #(.width(32)) multiplexer_14 (
    .in0(undriven), .in1(bit_extender_6_out), .out(multiplexer_14_out), .sel(LB));
  assign bit_extender_6_out = {{24{1'b1}}, multiplexer_13_out};  // Bit_Extender bit_extender_6
  Multiplexer #(.width(32)) multiplexer_15 (
    .in0({alu_1_result_2, alu_1_result}), .in1(cache_1_readdata), .out(multiplexer_15_out),
    .sel(controller_1_memtoreg));
endmodule
